# Fritzing sketch Smart Lighting PIR Interface (saved by Fritzing 1.0.7)
stripboards: 1

parts:
  L_sens_SL_N = Camdenboss CTB0158-3 [part_number=CTB0158-3 package=THT]
  L_in_N = Camdenboss CTB0158-2 [part_number=CTB0158-2 package=THT]
  J6 = Camdenboss CTB0158-6 [part_number=CTB0158-6 package=THT]
  Pwr_led = Camdenboss CTB0158-2 [part_number=CTB0158-2 package=THT]  # not connected
  Trig_Sw = Camdenboss CTB0158-2 [part_number=CTB0158-2 package=THT]
  Trig_LED = Camdenboss CTB0158-2 [part_number=CTB0158-2 package=THT]
  U1 = DS2Y-5-DC5V [part_number=DS2Y-5-DC5V]  # not connected
  F1 = FUSE [package=fuse_5mm]
  VR1 = XL4005 [part_number=XL4005 package=TO263]  # not connected
  C1 = Film/Foil Capacitor [capacitance=100nF voltage=35V package="27.5mm [THT, pp]"]  # not connected
  56YM1 = Namvo CP080011 PSU [mpn=56YSM10-0502000]
  L_Out_N = Camdenboss CTB0158-2 [part_number=CTB0158-2 package=THT]
  D1 = Diode [part_number=1N4007 package=diode-hv]
  F2 = FUSE [package=fuse_5mm]

nets:
  N1: L_sens_SL_N.pin1, J6.pin4, J6.pin5, Trig_Sw.pin2, F1.2
  N2: L_sens_SL_N.pin2, Trig_Sw.pin1, Trig_LED.pin1, 56YM1.AC/L
  N3: L_sens_SL_N.pin3, L_in_N.pin2, J6.pin2, Trig_LED.pin2, 56YM1.AC/N, L_Out_N.pin2
  N4: L_in_N.pin1, F1.1
  N5: J6.pin3, L_Out_N.pin1
  N6: J6.pin6, D1.C
  N7: F2.1, F2.2

custom parts:
  Namvo CP080011 PSU: Namvo 2pcs AC DC Switching Power Supply Module, AC 220V To DC 5V Micro Volume Isolated Switching Power Supply Board Isolated Regulated Power Supply Module
